# Fritzing sketch mosquito (saved by Fritzing 1.0.4)
breadboards: 1

parts:
  Mod1 = Passive Buzzer
  WeMos_D1_Mini1 = WeMos D1 Mini
  Mod2 = KY-018 Photoresistor Module [package="Breakout board"]

nets:
  N1: Mod1.S, WeMos_D1_Mini1.G, Mod2.-
  N2: Mod1.-, WeMos_D1_Mini1.D2
  3V3: WeMos_D1_Mini1.3V3, Mod2.Vin
  N3: WeMos_D1_Mini1.A0, Mod2.S

custom parts:
  KY-018 Photoresistor Module: KY-018 Photoresistor module, used to measure light intensity. It can determine the presence or absence of light.
